# Fritzing sketch esp32-cam-motion (saved by Fritzing 0.9.6b)

parts:
  ESP32_-_Back1 = ESP32 - CAM
  J1 = Infrared Proximity Sensor

nets:
  N1: ESP32_-_Back1.GPIO12, J1.Vout
  3.3V: ESP32_-_Back1.3.3V, J1.Vcc
  GND: ESP32_-_Back1.GND, J1.GND

custom parts:
  ESP32 - CAM: The ESP32-CAM has a very competitive small-size camera module that can operate independently as a minimum system with a footprint of only 27*40.5*4.5mm and a deep sleep current of up to 6mA.
